// Logisim project MIPSprocessor_Minimal.circ as structural Verilog: 8 circuits, main circuit Main
module Main (
  input  Reset
);

  wire Alu_eq, Id_branch, Id_memread, Id_memwrite;
  wire [2:0] Id_aluop;
  wire [31:0] Alu_output, Id_reg1data, Id_reg2data, Id_secondreg, if_instructions, Mem_output;

  \if  \if  (.eq(Alu_eq), .branch(Id_branch), .offset(Id_reg2data), .Reset(Reset), .Instructions(if_instructions));
  Id Id (
    .writeRegData(Alu_output), .writeMemData(Mem_output), .Instruction(if_instructions), .Reset(Reset),
    .reg1Data(Id_reg1data), .secondReg(Id_secondreg), .reg2Data(Id_reg2data), .ALUOp(Id_aluop),
    .memRead(Id_memread), .memWrite(Id_memwrite), .branch(Id_branch));
  Alu Alu (
    .reg1Data(Id_reg1data), .reg2Data(Id_reg2data), .op(Id_aluop), .secondReg(Id_secondreg),
    .\output (Alu_output), .eq(Alu_eq));
  Mem Mem (.addr(Alu_output), .write(Id_memwrite), .read(Id_memread), .\input (Id_secondreg), .\output (Mem_output));

  // Notes on the sheet:
  //   Test Code
  //   nor $1, $0, $0 # $1=-1
  //   sub $2, $0, $1 #2 = 1
  //   add $3, $2, $2 # $3 =2
  //   addi $1, $0, 8 # $1 = 8
  //   slt $4, $2, $3
  //   beq $4, $2, 2
  //   addi $6, $0, 0
  //   addi $6, $0, 12
  //   sw $4, 0($1)
  //   lw $5, 0($1)
  //   0x00000827 = 000000 00000 00000 00001 00000 100111
  //   0x00011022 = 000000 00000 00001 00010 00000 100010
  //   0x00421820 = 000000 00010 00010 00011 00000 100000
  //   0x20110008 = 0010 0000 0000 0001 0000 0000 0000 1000
  //   	0x0043202A = 000000 00010 00011 00100 00000 101010 
  //   0x10820002 = 000100 00100 00010 0000000000000010 
  //   0x20060000 = 001000 00000 00110 0000000000000000
  //   0x2006000C = 001000 00000 00110 0000000000001100
  //   0xAC240000 = 101011 00001 00100 0000000000000000
  //   0x8C250000 = 100011 00001 00101 0000000000000000
endmodule

module \if  (
  input  eq,
  input  branch,
  input  [31:0] offset,
  input  Reset,
  output [31:0] Instructions
);

  wire and_1_out, clock_1_out;
  wire [31:0] adder_1_out, adder_2_out, multiplexer_1_out, register_1_q, shifter_1_out;

  Clock clock_1 (.out(clock_1_out));
  Register #(.width(32)) register_1 (
    .D(multiplexer_1_out), .clk(clock_1_out), .Q(register_1_q), .clr(Reset));  // open: en
  and and_1 (and_1_out, eq, branch);
  Shifter #(.width(32)) shifter_1 (.in(offset), .\dist (5'b00010), .out(shifter_1_out));
  Adder #(.width(32)) adder_1 (.a(32'h4), .b(register_1_q), .out(adder_1_out));  // open: cin, cout
  ROM #(.dataWidth(32)) rom_1 (.addr(register_1_q[9:2]), .data(Instructions));
  Multiplexer #(.width(32), .enable("false")) multiplexer_1 (
    .in0(adder_1_out), .in1(adder_2_out), .out(multiplexer_1_out), .sel(and_1_out));
  Adder #(.width(32)) adder_2 (.a(shifter_1_out), .b(adder_1_out), .out(adder_2_out));  // open: cin, cout

  // Notes on the sheet:
  //   contents of rom_1 (hex, n*v repeats v):
  //   827 11022 421820 20010008 43202a 10820002 20060000 2006000c ac240000 8c250000
  //   Instruction Fetch
endmodule

module Id (
  input  [31:0] writeRegData,
  input  [31:0] writeMemData,
  input  [31:0] Instruction,
  input  Reset,
  output [31:0] reg1Data,
  output [31:0] secondReg,
  output [31:0] reg2Data,
  output [2:0] ALUOp,
  output memRead,
  output memWrite,
  output branch
);

  wire [2:0] rom_2_data, rom_3_data;
  wire [4:0] multiplexer_1_out;
  wire [5:1] rom_1_data;
  wire [31:0] bit_extender_1_out, multiplexer_2_out;

  Multiplexer #(.width(5), .enable("false")) multiplexer_1 (
    .in0(Instruction[15:11]), .in1(Instruction[20:16]), .out(multiplexer_1_out), .sel(rom_1_data[4]));
  ROM #(.addrWidth(6), .dataWidth(6)) rom_1 (
    .addr(Instruction[31:26]), .data({rom_1_data[5:4], memRead, memWrite, rom_1_data[1], branch}));
  Multiplexer #(.width(32), .enable("false")) multiplexer_2 (
    .in0(writeRegData), .in1(writeMemData), .out(multiplexer_2_out), .sel(rom_1_data[1]));
  Registerfile Registerfile (
    .WriteData(multiplexer_2_out), .reg1(Instruction[25:21]), .reg2(Instruction[20:16]),
    .WriteReg(multiplexer_1_out), .RegWrite(rom_1_data[5]), .Reset(Reset), .out_7(reg1Data), .out_8(secondReg));
  assign bit_extender_1_out = {{16{Instruction[15]}}, Instruction[15:0]};  // Bit_Extender bit_extender_1
  ROM #(.addrWidth(6), .dataWidth(3)) rom_2 (.addr(Instruction[5:0]), .data(rom_2_data));
  ROM #(.addrWidth(6), .dataWidth(3)) rom_3 (.addr(Instruction[31:26]), .data(rom_3_data));
  Multiplexer #(.width(32), .enable("false")) multiplexer_3 (
    .in0(secondReg), .in1(bit_extender_1_out), .out(reg2Data), .sel(rom_1_data[4]));
  Multiplexer #(.width(3), .enable("false")) multiplexer_4 (
    .in0(rom_2_data), .in1(rom_3_data), .out(ALUOp), .sel(rom_1_data[4]));

  // Notes on the sheet:
  //   R-format
  //   func
  //   shamt
  //   rd
  //   rt
  //   rs
  //   op
  //   contents of rom_1 (hex, n*v repeats v):
  //   20 0 0 0 1 0 0 0 30 0 0 0 30 22*0 3a 7*0 14
  //   RegisterWrite
  //   RegToMem
  //   contents of rom_2 (hex, n*v repeats v):
  //   34*0 1 4*0 6 0 0 3
  //   contents of rom_3 (hex, n*v repeats v):
  //   12*0 4 21*0 1 4*0 6 0 0 3
  //   ALUSrc
  //   add: 10 0000 = 20| op= 0
  //   nor: 10 0111 = 27 | op= 6
  //   sub:  10 0010 = 22 | op= 1
  //   slt: 10 1010 = 2a | op= 3
  //   addi: 00 1000 | op = 0
  //   andi: 00 1100 | op = 4
  //   lw: 10 0011 | op = 0 
  //   sw: 10 1011 | op = 0
  //   beq 00 0100 | op = XX
  //   R-format:   1            0            0             0            0             0
  //   I-format:   1            1            0             0            0             0
  //             lw:   1            1            1             0            1             0
  //            sw:   0            1            0             1            X             0
  //           branch:   0            X            0             0            X             1
  //   RegWrite ALUSrc MemRead MemWrite RegToMem Branch
endmodule

module Registerfile (
  input  [31:0] WriteData,
  input  [4:0] reg1,
  input  [4:0] reg2,
  input  [4:0] WriteReg,
  input  RegWrite,
  input  Reset,
  output [31:0] out_7,
  output [31:0] out_8
);

  wire demultiplexer_1_out0, demultiplexer_1_out1;
  wire [31:0] register16_1_readdata1, register16_1_readdata2, register16_2_readdata1, register16_2_readdata2;

  Demultiplexer #(.enable("false")) demultiplexer_1 (
    .out0(demultiplexer_1_out0), .out1(demultiplexer_1_out1), .in(RegWrite), .sel(WriteReg[4]));
  register16 register16_1 (
    .WriteData(WriteData), .reg1(reg1[3:0]), .reg2(reg2[3:0]), .WriteReg(WriteReg[3:0]),
    .RegWrite(demultiplexer_1_out0), .Reset(Reset), .readData1(register16_1_readdata1),
    .readData2(register16_1_readdata2));
  register16 register16_2 (
    .WriteData(WriteData), .reg1(reg1[3:0]), .reg2(reg2[3:0]), .WriteReg(WriteReg[3:0]),
    .RegWrite(demultiplexer_1_out1), .Reset(Reset), .readData1(register16_2_readdata1),
    .readData2(register16_2_readdata2));
  Multiplexer #(.width(32), .enable("false")) multiplexer_1 (
    .in0(register16_1_readdata1), .in1(register16_2_readdata1), .out(out_7), .sel(reg1[4]));
  Multiplexer #(.width(32), .enable("false")) multiplexer_2 (
    .in0(register16_1_readdata2), .in1(register16_2_readdata2), .out(out_8), .sel(reg2[4]));
endmodule

module register16 (
  input  [31:0] WriteData,
  input  [3:0] reg1,
  input  [3:0] reg2,
  input  [3:0] WriteReg,
  input  RegWrite,
  input  Reset,
  output [31:0] readData1,
  output [31:0] readData2
);

  wire demultiplexer_1_out0, demultiplexer_1_out1, demultiplexer_1_out2, demultiplexer_1_out3;
  wire [31:0] register4_1_regdata1, register4_1_regdata2, register4_2_regdata1, register4_2_regdata2,
       register4_3_regdata1, register4_3_regdata2, register4_4_regdata1, register4_4_regdata2;

  Demultiplexer #(.select(2), .enable("false")) demultiplexer_1 (
    .out0(demultiplexer_1_out0), .out1(demultiplexer_1_out1), .out2(demultiplexer_1_out2),
    .out3(demultiplexer_1_out3), .in(RegWrite), .sel(WriteReg[3:2]));
  register4 register4_1 (
    .WriteData(WriteData), .reg1(reg1[1:0]), .RegWrite(demultiplexer_1_out0), .writeReg(WriteReg[1:0]),
    .reg2(reg2[1:0]), .Reset(Reset), .regData1(register4_1_regdata1), .regData2(register4_1_regdata2));
  register4 register4_2 (
    .WriteData(WriteData), .reg1(reg1[1:0]), .RegWrite(demultiplexer_1_out1), .writeReg(WriteReg[1:0]),
    .reg2(reg2[1:0]), .Reset(Reset), .regData1(register4_2_regdata1), .regData2(register4_2_regdata2));
  register4 register4_3 (
    .WriteData(WriteData), .reg1(reg1[1:0]), .RegWrite(demultiplexer_1_out2), .writeReg(WriteReg[1:0]),
    .reg2(reg2[1:0]), .Reset(Reset), .regData1(register4_3_regdata1), .regData2(register4_3_regdata2));
  register4 register4_4 (
    .WriteData(WriteData), .reg1(reg1[1:0]), .RegWrite(demultiplexer_1_out3), .writeReg(WriteReg[1:0]),
    .reg2(reg2[1:0]), .Reset(Reset), .regData1(register4_4_regdata1), .regData2(register4_4_regdata2));
  Multiplexer #(.select(2), .width(32), .enable("false")) multiplexer_1 (
    .in0(register4_1_regdata1), .in1(register4_2_regdata1), .in2(register4_3_regdata1),
    .in3(register4_4_regdata1), .out(readData1), .sel(reg1[3:2]));
  Multiplexer #(.select(2), .width(32), .enable("false")) multiplexer_2 (
    .in0(register4_1_regdata2), .in1(register4_2_regdata2), .in2(register4_3_regdata2),
    .in3(register4_4_regdata2), .out(readData2), .sel(reg2[3:2]));
endmodule

module register4 (
  input  [31:0] WriteData,
  input  [1:0] reg1,
  input  RegWrite,
  input  [1:0] writeReg,
  input  [1:0] reg2,
  input  Reset,
  output [31:0] regData1,
  output [31:0] regData2
);

  wire clock_1_out, clock_2_out, clock_3_out, clock_4_out, demultiplexer_1_out0, demultiplexer_1_out1,
       demultiplexer_1_out2, demultiplexer_1_out3;
  wire [31:0] register_1_q, register_2_q, register_3_q, register_4_q;

  Demultiplexer #(.select(2), .enable("false")) demultiplexer_1 (
    .out0(demultiplexer_1_out0), .out1(demultiplexer_1_out1), .out2(demultiplexer_1_out2),
    .out3(demultiplexer_1_out3), .in(RegWrite), .sel(writeReg));
  Clock clock_1 (.out(clock_1_out));
  Clock clock_2 (.out(clock_2_out));
  Clock clock_3 (.out(clock_3_out));
  Register #(.width(32)) register_1 (
    .D(WriteData), .en(demultiplexer_1_out0), .clk(clock_4_out), .Q(register_1_q), .clr(Reset));
  Clock clock_4 (.out(clock_4_out));
  Register #(.width(32)) register_2 (
    .D(WriteData), .en(demultiplexer_1_out1), .clk(clock_1_out), .Q(register_2_q), .clr(Reset));
  Register #(.width(32)) register_3 (
    .D(WriteData), .en(demultiplexer_1_out2), .clk(clock_2_out), .Q(register_3_q), .clr(Reset));
  Register #(.width(32)) register_4 (
    .D(WriteData), .en(demultiplexer_1_out3), .clk(clock_3_out), .Q(register_4_q), .clr(Reset));
  Multiplexer #(.select(2), .width(32), .enable("false")) multiplexer_1 (
    .in0(register_1_q), .in1(register_2_q), .in2(register_3_q), .in3(register_4_q), .out(regData1), .sel(reg1));
  Multiplexer #(.select(2), .width(32), .enable("false")) multiplexer_2 (
    .in0(register_1_q), .in1(register_2_q), .in2(register_3_q), .in3(register_4_q), .out(regData2), .sel(reg2));
endmodule

module Alu (
  input  [31:0] reg1Data,
  input  [31:0] reg2Data,
  input  [2:0] op,
  input  [31:0] secondReg,
  output [31:0] \output ,
  output eq
);

  wire [0:0] comparator_1_lt;
  wire [31:0] adder_1_out, and_1_out, nor_1_out, or_1_out, shifter_1_out, subtractor_1_out, xor_1_out;

  Adder #(.width(32)) adder_1 (.a(reg1Data), .b(reg2Data), .out(adder_1_out));  // open: cin, cout
  Subtractor #(.width(32)) subtractor_1 (.a(reg1Data), .b(reg2Data), .out(subtractor_1_out));  // open: bin, bout
  Shifter #(.width(32)) shifter_1 (.in(reg1Data), .\dist (reg2Data[4:0]), .out(shifter_1_out));
  Comparator #(.width(32)) comparator_1 (.a(reg1Data), .b(reg2Data), .lt(comparator_1_lt[0]));  // open: gt, eq
  assign and_1_out = reg1Data & reg2Data;  // AND_Gate and_1, 32 bits wide
  assign or_1_out = reg1Data | reg2Data;  // OR_Gate or_1, 32 bits wide
  assign nor_1_out = ~(reg1Data | reg2Data);  // NOR_Gate nor_1, 32 bits wide
  assign xor_1_out = reg1Data ^ reg2Data;  // XOR_Gate xor_1, 32 bits wide
  Comparator #(.width(32)) comparator_2 (.a(reg1Data), .b(secondReg), .eq(eq));  // open: gt, lt
  Multiplexer #(.select(3), .width(32), .enable("false")) multiplexer_1 (
    .in0(adder_1_out), .in1(subtractor_1_out), .in2(shifter_1_out), .in3({{31{1'b0}}, comparator_1_lt[0]}),
    .in4(and_1_out), .in5(or_1_out), .in6(nor_1_out), .in7(xor_1_out), .out(\output ), .sel(op));
endmodule

module Mem (
  input  [31:0] addr,
  input  write,
  input  read,
  input  [31:0] \input ,
  output [31:0] \output 
);

  wire clock_1_out;

  RAM #(.dataWidth(32), .databus("bibus")) ram_1 (
    .addr(addr[9:2]), .we(write), .oe(read), .clk(clock_1_out), .din(\input ), .dout(\output ));
  Clock clock_1 (.out(clock_1_out));
endmodule
